# Fritzing sketch schematic (saved by Fritzing 0.9.4)
breadboards: 1

parts:
  Nano = Arduino Nano (Rev3.0)
  R1 = Temperature Sensor (Thermistor) [thermistor_type=NTC package=THT]
  R2 = Resistor [tolerance=±5% resistance=10k package=THT]
  C1 = Ceramic Capacitor [capacitance="100 nF" package="0805 [SMD, multilayer]"]
  JP1 = Header 3 [part_number=1-Wire package=1x03-1mm-ra]

nets:
  GND: Nano.GND, R1.pin_0, C1.0, JP1.3
  N1: Nano.D12/MISO, JP1.2
  N2: Nano.5V, R2.Pin_1, JP1.1
  N3: Nano.A1, R1.pin_1, R2.Pin_0, C1.1
